# Fritzing sketch LuceIngresso (saved by Fritzing 0.4.1b)
breadboards: 1

parts:
  Arduino2009 = Arduino
  SENSORIR = Infrared Proximity Sensor
  SENSORLUM = Photocell (LDR) [package=THT]  # not connected
  R2 = Resistor [resistance=220 package=THT]
  ULN2003A = ULN2003A
  Power_plug1 = Power plug
  RGB_Strip1 = Generic female header - 4 pins [form="♀ (female)"]
  J1 = Piezo Speaker

nets:
  GND: Arduino2009.GND, SENSORIR.GND, ULN2003A.connector7, Power_plug1.GND, J1.pin1
  N1: Arduino2009.D9, J1.pin2
  N2: Arduino2009.D6, ULN2003A.connector0
  N3: Arduino2009.D5, ULN2003A.connector1
  N4: Arduino2009.D3, ULN2003A.connector2
  +5V: Arduino2009.+5V, SENSORIR.Vcc
  N5: Arduino2009.A0, R2.Pin_0
  N6: Arduino2009.A5, SENSORIR.Vout
  N7: ULN2003A.connector13, RGB_Strip1.connector3
  N8: ULN2003A.connector14, RGB_Strip1.connector2
  N9: ULN2003A.connector15, RGB_Strip1.connector1
  N10: Power_plug1.VCC, RGB_Strip1.connector0

notes:
  Sensore di prossimità Sharp GP2Y0A21YK
  Arduino Source code: http://github.com/amedeos/LuceInIngresso/blob/master/LuceIngresso/LuceIngresso.pde
  Alimentatore 12V 500mA
  Seven Darlington Array
  ULN2003A
